// Logisim project booth part 3.circ as structural Verilog: 1 circuit, main circuit main
module main (
  input  [1:0] in_1,
  input  in_2,
  input  in_3,
  input  [7:0] in_4,
  input  in_5,
  input  in_6,
  output out_7,
  output [15:0] out_8,
  output [15:0] out_9
);

  wire adder_2_cout, adder_3_cout, adder_4_cout, adder_5_cout, adder_6_cout, adder_7_cout, and_1_out,
       button_1_out, button_2_out, clock_1_out, d_ff_2_q, d_ff_4_q, d_ff_6_q, d_ff_8_q, d_ff_10_q, d_ff_12_q,
       d_ff_14_q, d_ff_16_q, demultiplexer_1_out0, demultiplexer_1_out1, demultiplexer_1_out2,
       demultiplexer_1_out3, demultiplexer_1_out4, demultiplexer_1_out5, demultiplexer_1_out6,
       demultiplexer_1_out7;
  wire [1:0] comparator_1_gt, comparator_2_gt, multiplexer_1_out;
  wire [2:0] j_k_ff_3_q;
  wire [7:0] adder_1_out, d_ff_15_q, d_ff_15_qn, multiplexer_2_out, ram_1_data;
  wire [7:7] bitselector_1_out;
  wire [15:0] adder_2_out, adder_3_out, adder_4_out, adder_5_out, adder_6_out, adder_7_out,
       demultiplexer_2_out0, demultiplexer_2_out1, demultiplexer_2_out2, demultiplexer_2_out3,
       demultiplexer_2_out4, demultiplexer_2_out5, demultiplexer_2_out6, demultiplexer_2_out7, register_1_q,
       register_2_q, register_3_q, register_4_q, register_5_q, register_6_q, register_7_q, register_8_q,
       shifter_1_out;

  Button button_1 (.out(button_1_out));
  Button button_2 (.out(button_2_out));
  RAM #(.addrWidth(2), .bus("separate")) ram_1 (
    .addr(in_1), .din(in_4), .data(ram_1_data), .str(in_2), .sel(1'b1), .clk(button_2_out), .ld(in_3));  // open: clr
  D_Flip_Flop d_ff_1 (
    .clk(button_2_out), .D(ram_1_data[7]), .Q(d_ff_15_q[7]), .Qn(d_ff_15_qn[7]));  // open: preset, en, reset
  D_Flip_Flop d_ff_2 (.clk(button_1_out), .D(in_5), .Q(d_ff_2_q));  // open: Qn, preset, en, reset
  D_Flip_Flop d_ff_3 (
    .clk(button_2_out), .D(ram_1_data[6]), .Q(d_ff_15_q[6]), .Qn(d_ff_15_qn[6]));  // open: preset, en, reset
  D_Flip_Flop d_ff_4 (.clk(button_1_out), .D(d_ff_2_q), .Q(d_ff_4_q));  // open: Qn, preset, en, reset
  and and_1 (and_1_out, j_k_ff_3_q[1], j_k_ff_3_q[0]);
  J_K_Flip_Flop j_k_ff_1 (
    .J(and_1_out), .clk(button_1_out), .K(and_1_out), .Q(j_k_ff_3_q[2]));  // open: Qn, preset, en, reset
  D_Flip_Flop d_ff_5 (
    .clk(button_2_out), .D(ram_1_data[5]), .Q(d_ff_15_q[5]), .Qn(d_ff_15_qn[5]));  // open: preset, en, reset
  D_Flip_Flop d_ff_6 (.clk(button_1_out), .D(d_ff_4_q), .Q(d_ff_6_q));  // open: Qn, preset, en, reset
  J_K_Flip_Flop j_k_ff_2 (
    .J(j_k_ff_3_q[0]), .clk(button_1_out), .K(j_k_ff_3_q[0]), .Q(j_k_ff_3_q[1]));  // open: Qn, preset, en, reset
  D_Flip_Flop d_ff_7 (
    .clk(button_2_out), .D(ram_1_data[4]), .Q(d_ff_15_q[4]), .Qn(d_ff_15_qn[4]));  // open: preset, en, reset
  D_Flip_Flop d_ff_8 (.clk(button_1_out), .D(d_ff_6_q), .Q(d_ff_8_q));  // open: Qn, preset, en, reset
  J_K_Flip_Flop j_k_ff_3 (.J(1'b1), .clk(button_1_out), .K(1'b1), .Q(j_k_ff_3_q[0]));  // open: Qn, preset, en, reset
  D_Flip_Flop d_ff_9 (
    .clk(button_2_out), .D(ram_1_data[3]), .Q(d_ff_15_q[3]), .Qn(d_ff_15_qn[3]));  // open: preset, en, reset
  D_Flip_Flop d_ff_10 (.clk(button_1_out), .D(d_ff_8_q), .Q(d_ff_10_q));  // open: Qn, preset, en, reset
  D_Flip_Flop d_ff_11 (
    .clk(button_2_out), .D(ram_1_data[2]), .Q(d_ff_15_q[2]), .Qn(d_ff_15_qn[2]));  // open: preset, en, reset
  D_Flip_Flop d_ff_12 (.clk(button_1_out), .D(d_ff_10_q), .Q(d_ff_12_q));  // open: Qn, preset, en, reset
  D_Flip_Flop d_ff_13 (
    .clk(button_2_out), .D(ram_1_data[1]), .Q(d_ff_15_q[1]), .Qn(d_ff_15_qn[1]));  // open: preset, en, reset
  D_Flip_Flop d_ff_14 (.clk(button_1_out), .D(d_ff_12_q), .Q(d_ff_14_q));  // open: Qn, preset, en, reset
  D_Flip_Flop d_ff_15 (
    .clk(button_2_out), .D(ram_1_data[0]), .Q(d_ff_15_q[0]), .Qn(d_ff_15_qn[0]));  // open: preset, en, reset
  Adder adder_1 (.a(d_ff_15_qn), .b(8'h1), .out(adder_1_out));  // open: cin, cout
  D_Flip_Flop d_ff_16 (.clk(button_1_out), .D(d_ff_14_q), .Q(d_ff_16_q));  // open: Qn, preset, en, reset
  Comparator #(.width(1), .mode("unsigned")) comparator_1 (
    .a(d_ff_14_q), .b(d_ff_16_q), .gt(comparator_1_gt[0]), .eq(comparator_1_gt[1]));  // open: lt
  Comparator #(.width(1), .mode("unsigned")) comparator_2 (
    .a(d_ff_16_q), .b(1'b0), .gt(comparator_2_gt[0]), .eq(comparator_2_gt[1]));  // open: lt
  Multiplexer #(.width(2), .enable("false")) multiplexer_1 (
    .in0(comparator_2_gt), .in1(comparator_1_gt), .out(multiplexer_1_out), .sel(in_6));
  Multiplexer #(.select(2), .width(8), .enable("false")) multiplexer_2 (
    .in0(d_ff_15_q), .in1(adder_1_out), .in2({8{1'b0}}), .in3({8{1'b0}}), .out(multiplexer_2_out),
    .sel(multiplexer_1_out));
  Demultiplexer #(.select(3), .enable("false")) demultiplexer_1 (
    .out0(demultiplexer_1_out0), .out1(demultiplexer_1_out1), .out2(demultiplexer_1_out2),
    .out3(demultiplexer_1_out3), .out4(demultiplexer_1_out4), .out5(demultiplexer_1_out5),
    .out6(demultiplexer_1_out6), .out7(demultiplexer_1_out7), .in(1'b1), .sel(j_k_ff_3_q));
  BitSelector bitselector_1 (.in(multiplexer_2_out), .out(bitselector_1_out[7]), .sel(3'b111));
  Clock clock_1 (.out(clock_1_out));
  Demultiplexer #(.select(3), .width(16), .enable("false")) demultiplexer_2 (
    .out0(demultiplexer_2_out0), .out1(demultiplexer_2_out1), .out2(demultiplexer_2_out2),
    .out3(demultiplexer_2_out3), .out4(demultiplexer_2_out4), .out5(demultiplexer_2_out5),
    .out6(demultiplexer_2_out6), .out7(demultiplexer_2_out7), .in(shifter_1_out), .sel(j_k_ff_3_q));
  Shifter #(.width(16)) shifter_1 (
    .in({{8{bitselector_1_out[7]}}, multiplexer_2_out}), .\dist ({1'b0, j_k_ff_3_q}), .out(shifter_1_out));
  Register #(.width(16)) register_1 (
    .D(demultiplexer_2_out0), .en(demultiplexer_1_out0), .Q(register_1_q), .clk(clock_1_out));  // open: clr
  Register #(.width(16)) register_2 (
    .D(demultiplexer_2_out1), .en(demultiplexer_1_out1), .Q(register_2_q), .clk(clock_1_out));  // open: clr
  Register #(.width(16)) register_3 (
    .D(demultiplexer_2_out2), .en(demultiplexer_1_out2), .Q(register_3_q), .clk(clock_1_out));  // open: clr
  Register #(.width(16)) register_4 (
    .D(demultiplexer_2_out3), .en(demultiplexer_1_out3), .Q(register_4_q), .clk(clock_1_out));  // open: clr
  Register #(.width(16)) register_5 (
    .D(demultiplexer_2_out4), .en(demultiplexer_1_out4), .Q(register_5_q), .clk(clock_1_out));  // open: clr
  Register #(.width(16)) register_6 (
    .D(demultiplexer_2_out5), .en(demultiplexer_1_out5), .Q(register_6_q), .clk(clock_1_out));  // open: clr
  Register #(.width(16)) register_7 (
    .D(demultiplexer_2_out6), .en(demultiplexer_1_out6), .Q(register_7_q), .clk(clock_1_out));  // open: clr
  Register #(.width(16)) register_8 (
    .D(demultiplexer_2_out7), .en(demultiplexer_1_out7), .Q(register_8_q), .clk(clock_1_out));  // open: clr
  Adder #(.width(16)) adder_2 (
    .a(register_1_q), .b(register_2_q), .out(adder_2_out), .cout(adder_2_cout));  // open: cin
  Adder #(.width(16)) adder_3 (
    .a(adder_2_out), .b(register_3_q), .out(adder_3_out), .cin(adder_2_cout), .cout(adder_3_cout));
  Adder #(.width(16)) adder_4 (
    .a(adder_3_out), .b(register_4_q), .out(adder_4_out), .cin(adder_3_cout), .cout(adder_4_cout));
  Adder #(.width(16)) adder_5 (
    .a(adder_4_out), .b(register_5_q), .out(adder_5_out), .cin(adder_4_cout), .cout(adder_5_cout));
  Adder #(.width(16)) adder_6 (
    .a(adder_5_out), .b(register_6_q), .out(adder_6_out), .cin(adder_5_cout), .cout(adder_6_cout));
  Adder #(.width(16)) adder_7 (
    .a(adder_6_out), .b(register_7_q), .out(adder_7_out), .cin(adder_6_cout), .cout(adder_7_cout));
  Adder #(.width(16)) adder_8 (.a(adder_7_out), .b(register_8_q), .out(out_8), .cin(adder_7_cout), .cout(out_7));
  Subtractor #(.width(16)) subtractor_1 (.a(out_8), .b(16'h1), .out(out_9));  // open: bin, bout

  // Notes on the sheet:
  //   Memory
  //   Counter
  //   Multiplicand
  //   Multiplier
  //   Left Shifter
  //   Final Result
endmodule
